# Fritzing sketch Pipeline - Esquematização (saved by Fritzing 0.9.2b)
breadboards: 4

parts:
  LCD1 = LCD screen
  R1 = Rotary Potentiometer (Small) [maximum_resistance=100kΩ package=THT]
  Componente1 = Arduino Board Ethernet
  Componente2 = Arduino Uno (Rev3)  # not connected
  Componente3 = Arduino Uno (Rev3)
  LCD2 = LCD screen
  R2 = Rotary Potentiometer (Small) [maximum_resistance=100kΩ package=THT]
  Componente4 = Arduino Uno (Rev3)
  LCD3 = LCD screen
  R3 = Rotary Potentiometer (Small) [maximum_resistance=100kΩ package=THT]
  Componente5 = Arduino Uno (Rev3)  # not connected
  Componente6 = Arduino Board Ethernet
  LCD4 = LCD screen
  R4 = Rotary Potentiometer (Small) [maximum_resistance=100kΩ package=THT]
  Componente7 = Arduino Uno (Rev3)

nets:
  VSS: LCD1.VSS, LCD1.R/W, LCD1.LED-, R1.leg2, Componente1.GND
  VDD: LCD1.VDD, LCD1.LED+, R1.leg1, Componente1.5V
  N1: LCD1.V0, R1.wiper
  N2: LCD1.RS, Componente1.D9_PWM
  N3: LCD1.E, Componente1.D8
  N4: LCD1.DB4, Componente1.D5_PWM
  N5: LCD1.DB5, Componente1.D6_PWM
  N6: LCD1.DB6, Componente1.D3_PWM
  N7: LCD1.DB7, Componente1.D2_PWM
  N8: Componente1.D0/RX, Componente7.D1/TX
  N9: Componente1.D1/TX, Componente3.D0/RX
  N10: Componente3.D8, LCD2.E
  N11: Componente3.D9_PWM, LCD2.RS
  N12: Componente3.D10_PWM/SS, Componente6.D1/TX
  N13: Componente3.D12/MISO, Componente7.D2
  N14: Componente3.D1/TX, Componente4.D0/RX
  N15: Componente3.D2, LCD2.DB7
  N16: Componente3.D3_PWM, LCD2.DB6
  N17: Componente3.D5_PWM, LCD2.DB4
  N18: Componente3.D6_PWM, LCD2.DB5
  5V: Componente3.5V, LCD2.VDD, LCD2.LED+, R2.leg1
  GND: Componente3.GND, LCD2.VSS, LCD2.R/W, LCD2.LED-, R2.leg2
  N19: LCD2.V0, R2.wiper
  N20: Componente4.D8, LCD3.E
  N21: Componente4.D9_PWM, LCD3.RS
  N22: Componente4.D11_PWM/MOSI, Componente7.D0/RX
  N23: Componente4.D1/TX, Componente6.D0/RX
  N24: Componente4.D2, LCD3.DB7
  N25: Componente4.D3_PWM, LCD3.DB6
  N26: Componente4.D5_PWM, LCD3.DB4
  N27: Componente4.D6_PWM, LCD3.DB5
  5V_2: Componente4.5V, LCD3.VDD, LCD3.LED+, R3.leg1
  GND_2: Componente4.GND, LCD3.VSS, LCD3.R/W, LCD3.LED-, R3.leg2
  N28: LCD3.V0, R3.wiper
  N29: Componente6.D8, LCD4.E
  N30: Componente6.D9_PWM, LCD4.RS
  N31: Componente6.D2_PWM, LCD4.DB7
  N32: Componente6.D3_PWM, LCD4.DB6
  N33: Componente6.D5_PWM, LCD4.DB4
  N34: Componente6.D6_PWM, LCD4.DB5
  5V_3: Componente6.5V, LCD4.VDD, LCD4.LED+, R4.leg1
  GND_3: Componente6.GND, LCD4.VSS, LCD4.R/W, LCD4.LED-, R4.leg2
  N35: LCD4.V0, R4.wiper

notes:
  Instruction Fetch
  Instruction Decoder
  Executor
  Data Memory
  Controller
