# Fritzing sketch pipeline (saved by Fritzing 0.9.2b)
breadboards: 4

parts:
  LCD1 = LCD screen
  R1 = Rotary Potentiometer (Small) [maximum_resistance=100kΩ package=THT]
  Componente1 = Arduino Board Ethernet
  Componente2 = Arduino Uno (Rev3)  # not connected
  Componente3 = Arduino Uno (Rev3)
  LCD2 = LCD screen
  R2 = Rotary Potentiometer (Small) [maximum_resistance=100kΩ package=THT]
  Componente4 = Arduino Uno (Rev3)
  LCD3 = LCD screen
  R3 = Rotary Potentiometer (Small) [maximum_resistance=100kΩ package=THT]
  Componente5 = Arduino Uno (Rev3)  # not connected
  Componente6 = Arduino Board Ethernet
  LCD4 = LCD screen
  R4 = Rotary Potentiometer (Small) [maximum_resistance=100kΩ package=THT]
  Componente7 = Arduino Uno (Rev3)  # not connected

nets:
  VSS: LCD1.VSS, LCD1.R/W, R1.leg2, Componente1.GND
  VDD: LCD1.VDD, R1.leg1, Componente1.5V
  N1: LCD1.V0, R1.wiper
  N2: LCD1.RS, Componente1.D12/MISO
  N3: LCD1.E, Componente1.D11/MOSI
  N4: LCD1.DB4, Componente1.D6_PWM
  N5: LCD1.DB5, Componente1.D5_PWM
  N6: LCD1.DB6, Componente1.D3_PWM
  N7: LCD1.DB7, Componente1.D2_PWM
  N8: Componente3.D11_PWM/MOSI, LCD2.E
  N9: Componente3.D12/MISO, LCD2.RS
  N10: Componente3.D2, LCD2.DB7
  N11: Componente3.D3_PWM, LCD2.DB6
  N12: Componente3.D5_PWM, LCD2.DB5
  N13: Componente3.D6_PWM, LCD2.DB4
  5V: Componente3.5V, LCD2.VDD, R2.leg1
  GND: Componente3.GND, LCD2.VSS, LCD2.R/W, R2.leg2
  N14: LCD2.V0, R2.wiper
  N15: Componente4.D11_PWM/MOSI, LCD3.E
  N16: Componente4.D12/MISO, LCD3.RS
  N17: Componente4.D2, LCD3.DB7
  N18: Componente4.D3_PWM, LCD3.DB6
  N19: Componente4.D5_PWM, LCD3.DB5
  N20: Componente4.D6_PWM, LCD3.DB4
  5V_2: Componente4.5V, LCD3.VDD, R3.leg1
  GND_2: Componente4.GND, LCD3.VSS, LCD3.R/W, R3.leg2
  N21: LCD3.V0, R3.wiper
  N22: Componente6.D11/MOSI, LCD4.E
  N23: Componente6.D12/MISO, LCD4.RS
  N24: Componente6.D2_PWM, LCD4.DB7
  N25: Componente6.D3_PWM, LCD4.DB6
  N26: Componente6.D5_PWM, LCD4.DB5
  N27: Componente6.D6_PWM, LCD4.DB4
  5V_3: Componente6.5V, LCD4.VDD, R4.leg1
  GND_3: Componente6.GND, LCD4.VSS, LCD4.R/W, R4.leg2
  N28: LCD4.V0, R4.wiper
